// Logisim project NAND.circ as structural Verilog
module NAND_Gate (
  input  A,
  input  B
);

  wire nand_1_out;

  nand nand_1 (nand_1_out, A, B);
  LED led_1 (.in(nand_1_out));
endmodule

module NOT_Gate (
  input  A,
  output Q
);

  nand nand_1 (Q, A, A);
endmodule

module AND_Gate (
  input  A,
  input  B,
  input  C,
  output Q
);

  and and_1 (Q, A, B, C);
endmodule

module OR_Gate (
  input  A,
  input  B,
  output Q
);

  or or_1 (Q, A, B);
endmodule

module XOR_Gate (
  input  A,
  input  B,
  output Q
);

  xor xor_1 (Q, A, B);
endmodule
